# Fritzing sketch structure.sketch (saved by Fritzing 0.9.3b)
breadboards: 1

parts:
  S1 = Pushbutton [package="[THT]"]
  Part1 = Arduino Board Ethernet
  J1 = Piezo Speaker
  R1 = Resistor [tolerance=±5% resistance=220 package=THT]
  R2 = Resistor [tolerance=±5% resistance=220 package="2010 [SMD]"]
  D1 = LTE-302 [package=lte-302]
  Part3 = Altitude/Pressure Sensor - MPL3115A2 Breakout [part_number=SEN-11084]

nets:
  N1: S1.Pin_3, S1.Pin_4, Part1.D2_PWM, Part1.5V
  N2: Part1.GND, J1.pin1, R1.Pin_0, D1.A
  N3: Part1.A5, Part3.SDA
  N4: Part1.D4, R2.Pin_0
  N5: Part1.D5_PWM, J1.pin2
  N6: R2.Pin_1, D1.C

notes:
  Not the right BMP. You said this was okay instead.
